// Logisim project PLD.circ as structural Verilog: 36 circuits, main circuit PCBUS
module PCBUS (
  input  t0,
  input  t2,
  output PC_BUS
);

  or or_1 (PC_BUS, t0, t2);
endmodule

module ARLD (
  input  t0,
  input  t2,
  input  t4,
  input  clock,
  input  d1,
  input  d2,
  output AR_LD
);

  wire and_1_out, not_1_out, or_1_out, or_2_out;

  not not_1 (not_1_out, clock);
  or or_1 (or_1_out, d1, d2);
  and and_1 (and_1_out, t4, or_1_out);
  or or_2 (or_2_out, t0, t2, and_1_out);
  and and_2 (AR_LD, or_2_out, not_1_out);
endmodule

module PCLD (
  input  t4,
  input  clock,
  input  d5,
  input  d6,
  input  z,
  output PC_LD
);

  wire and_1_out, not_1_out, or_1_out;

  not not_1 (not_1_out, clock);
  or or_1 (or_1_out, d5, and_1_out);
  and and_1 (and_1_out, d6, z);
  and and_2 (PC_LD, t4, or_1_out, not_1_out);
endmodule

module PCINC (
  input  t1,
  input  t3,
  input  clock,
  input  d1,
  input  d2,
  input  d6,
  input  z,
  output PC_INC
);

  wire pc_inc0_1_pcinc0, pc_inc1_1_pcinc1;

  PC_INC0 pc_inc0_1 (.t1(t1), .t3(t3), .clock(clock), .d1(d1), .d2(d2), .PCINC0(pc_inc0_1_pcinc0));
  PC_INC1 pc_inc1_1 (.t3(t3), .clock(clock), .d6(d6), .z(z), .PCINC1(pc_inc1_1_pcinc1));
  or or_1 (PC_INC, pc_inc0_1_pcinc0, pc_inc1_1_pcinc1);
endmodule

module RLD (
  input  t3,
  input  clock,
  input  d3,
  output R_LD
);

  wire not_1_out;

  not not_1 (not_1_out, clock);
  and and_1 (R_LD, t3, d3, not_1_out);
endmodule

module SLD (
  input  t3,
  input  clock,
  input  d0,
  output S_LD
);

  wire not_1_out;

  not not_1 (not_1_out, clock);
  and and_1 (S_LD, t3, d0, not_1_out);
endmodule

module RBUS (
  input  t3,
  input  d4,
  input  d8,
  input  d9,
  input  d12,
  input  d13,
  output R_BUS
);

  wire or_1_out;

  and and_1 (R_BUS, t3, or_1_out);
  or or_1 (or_1_out, d4, d8, d9, d12, d13);
endmodule

module ACCCLR (
  input  t3,
  input  d11,
  output ACC_CLR
);

  and and_1 (ACC_CLR, t3, d11);
endmodule

module ACCBUS (
  input  t3,
  input  t5,
  input  d2,
  input  d3,
  input  d7,
  output ACC_BUS
);

  wire and_1_out, and_2_out, or_1_out;

  or or_1 (or_1_out, d3, d7);
  and and_1 (and_1_out, t5, d2);
  and and_2 (and_2_out, t3, or_1_out);
  or or_2 (ACC_BUS, and_1_out, and_2_out);
endmodule

module ZLD (
  output Z_LD
);


  assign Z_LD = 1'b1;
endmodule

module OUTRLD (
  input  t3,
  input  clock,
  input  d7,
  output OUTR_LD
);

  wire not_1_out;

  not not_1 (not_1_out, clock);
  and and_1 (OUTR_LD, d7, t3, not_1_out);
endmodule

module RAMRW (
  input  t2,
  input  clock,
  input  d6,
  output RAM_WE
);

  wire not_1_out;

  not not_1 (not_1_out, clock);
  and and_1 (RAM_WE, d6, t2, not_1_out);
endmodule

module IRLD (
  input  t2,
  input  clock,
  output IR_LD
);

  wire not_1_out;

  not not_1 (not_1_out, clock);
  and and_1 (IR_LD, t2, not_1_out);
endmodule

module DRLD (
  input  t1,
  input  t3,
  input  t5,
  input  clock,
  input  d1,
  input  d2,
  input  d5,
  input  d6,
  input  z,
  output DR_LD
);

  wire drld0_1_dr_ld0, drld1_1_dr_ld1;

  DRLD0 drld0_1 (.t1(t1), .t3(t3), .t5(t5), .clock(clock), .d1(d1), .d2(d2), .DR_LD0(drld0_1_dr_ld0));
  DRLD1 drld1_1 (.t3(t3), .clock(clock), .d5(d5), .d6(d6), .z(z), .DR_LD1(drld1_1_dr_ld1));
  or or_1 (DR_LD, drld0_1_dr_ld0, drld1_1_dr_ld1);
endmodule

module DRBUS (
  input  t4,
  input  t6,
  input  d1,
  input  d2,
  input  d5,
  input  d6,
  input  z,
  output DR_BUS
);

  wire drbus0_1_dr_bus0, drbus1_1_dr_bus1;

  DRBUS0 drbus0_1 (.t4(t4), .t6(t6), .d1(d1), .d2(d2), .DR_BUs0(drbus0_1_dr_bus0));
  DRBUS1 drbus1_1 (.t4(t4), .d5(d5), .d6(d6), .z(z), .DR_BUS1(drbus1_1_dr_bus1));
  or or_1 (DR_BUS, drbus0_1_dr_bus0, drbus1_1_dr_bus1);
endmodule

module ACCLD (
  input  t3,
  input  t6,
  input  clock,
  input  d1,
  input  d4,
  input  d8,
  input  d9,
  input  d10,
  input  d12,
  input  d13,
  input  d14,
  input  d15,
  output ACC_LD
);

  wire acc_ld0_1_accld0, acc_ld1_1_accld1, acc_ld2_1_accld2;

  ACC_LD0 acc_ld0_1 (.t3(t3), .clock(clock), .d4(d4), .d8(d8), .d9(d9), .d10(d10), .ACCLD0(acc_ld0_1_accld0));
  ACC_LD1 acc_ld1_1 (.t3(t3), .clock(clock), .d12(d12), .d13(d13), .d14(d14), .d15(d15), .ACCLD1(acc_ld1_1_accld1));
  ACC_LD2 acc_ld2_1 (.t6(t6), .clock(clock), .d1(d1), .ACCLD2(acc_ld2_1_accld2));
  or or_1 (ACC_LD, acc_ld0_1_accld0, acc_ld1_1_accld1, acc_ld2_1_accld2);
endmodule

module ALU_SEL (
  input  d1,
  input  d4,
  input  d9,
  input  d10,
  input  d12,
  input  d13,
  input  d14,
  input  d15,
  output s0,
  output s1,
  output s2
);

  ALUSEL0 alusel0_1 (.d1(d1), .d4(d4), .d9(d9), .d13(d13), .d15(d15), .ALU_SEL0(s0));
  ALUSEL1 alusel1_1 (.d1(d1), .d4(d4), .d10(d10), .d14(d14), .d15(d15), .ALU_SEL1(s1));
  ALUSEL2 alusel2_1 (.d12(d12), .d13(d13), .d14(d14), .d15(d15), .ALU_SEL2(s2));
endmodule

module SCCLR (
  input  t4,
  input  t5,
  input  t7,
  input  d1,
  input  d2,
  input  d5,
  input  d6,
  input  z,
  output SC_CLR
);

  wire scclr0_1_sc_clr0, scclr1_1_sc_clr1;

  SCCLR0 scclr0_1 (.t4(t4), .d1(d1), .d2(d2), .d5(d5), .d6(d6), .z(z), .SC_CLR0(scclr0_1_sc_clr0));
  SCCLR1 scclr1_1 (.t5(t5), .t7(t7), .d5(d5), .d6(d6), .z(z), .SC_CLR1(scclr1_1_sc_clr1));
  or or_1 (SC_CLR, scclr0_1_sc_clr0, scclr1_1_sc_clr1);
endmodule

module RAMEN (
  input  t1,
  input  t3,
  input  t5,
  input  clock,
  input  d1,
  input  d2,
  input  d5,
  input  d6,
  input  z,
  output RAM_OE
);

  wire ram_oe0_1_ramoe0, ram_oe1_1_ramoe1, ram_oe2_1_ramoe2;

  RAM_OE0 ram_oe0_1 (.t1(t1), .t5(t5), .clock(clock), .d1(d1), .RAMOE0(ram_oe0_1_ramoe0));
  RAM_OE1 ram_oe1_1 (.t3(t3), .clock(clock), .d1(d1), .d2(d2), .d5(d5), .RAMOE1(ram_oe1_1_ramoe1));
  RAM_OE2 ram_oe2_1 (.t3(t3), .clock(clock), .d6(d6), .z(z), .RAMOE2(ram_oe2_1_ramoe2));
  or or_1 (RAM_OE, ram_oe0_1_ramoe0, ram_oe1_1_ramoe1, ram_oe2_1_ramoe2);
endmodule

module ALUSEL0 (
  input  d1,
  input  d4,
  input  d9,
  input  d13,
  input  d15,
  output ALU_SEL0
);

  or or_1 (ALU_SEL0, d1, d4, d9, d13, d15);
endmodule

module ALUSEL1 (
  input  d1,
  input  d4,
  input  d10,
  input  d14,
  input  d15,
  output ALU_SEL1
);

  or or_1 (ALU_SEL1, d1, d4, d10, d14, d15);
endmodule

module ALUSEL2 (
  input  d12,
  input  d13,
  input  d14,
  input  d15,
  output ALU_SEL2
);

  or or_1 (ALU_SEL2, d12, d13, d14, d15);
endmodule

module RAM_OE0 (
  input  t1,
  input  t5,
  input  clock,
  input  d1,
  output RAMOE0
);

  wire and_1_out, not_1_out, or_1_out;

  and and_1 (and_1_out, t5, d1);
  not not_1 (not_1_out, clock);
  or or_1 (or_1_out, t1, and_1_out);
  and and_2 (RAMOE0, not_1_out, or_1_out);
endmodule

module RAM_OE1 (
  input  t3,
  input  clock,
  input  d1,
  input  d2,
  input  d5,
  output RAMOE1
);

  wire not_1_out, or_1_out;

  not not_1 (not_1_out, clock);
  or or_1 (or_1_out, d1, d2, d5);
  and and_1 (RAMOE1, not_1_out, t3, or_1_out);
endmodule

module RAM_OE2 (
  input  t3,
  input  clock,
  input  d6,
  input  z,
  output RAMOE2
);

  wire not_1_out;

  not not_1 (not_1_out, clock);
  and and_1 (RAMOE2, t3, not_1_out, d6, z);
endmodule

module SCCLR0 (
  input  t4,
  input  d1,
  input  d2,
  input  d5,
  input  d6,
  input  z,
  output SC_CLR0
);

  wire and_1_out, nor_1_out;

  and and_1 (and_1_out, d6, z);
  nor nor_1 (nor_1_out, d1, d2, d5, and_1_out);
  and and_2 (SC_CLR0, t4, nor_1_out);
endmodule

module SCCLR1 (
  input  t5,
  input  t7,
  input  d5,
  input  d6,
  input  z,
  output SC_CLR1
);

  wire and_1_out, and_2_out, or_1_out;

  and and_1 (and_1_out, d6, z);
  or or_1 (or_1_out, d5, and_1_out);
  and and_2 (and_2_out, t5, or_1_out);
  or or_2 (SC_CLR1, t7, and_2_out);
endmodule

module DRLD0 (
  input  t1,
  input  t3,
  input  t5,
  input  clock,
  input  d1,
  input  d2,
  output DR_LD0
);

  wire and_1_out, not_1_out, or_1_out, or_2_out, or_3_out;

  or or_1 (or_1_out, t3, t5);
  or or_2 (or_2_out, d1, d2);
  not not_1 (not_1_out, clock);
  and and_1 (and_1_out, or_1_out, or_2_out);
  or or_3 (or_3_out, t1, and_1_out);
  and and_2 (DR_LD0, not_1_out, or_3_out);
endmodule

module DRLD1 (
  input  t3,
  input  clock,
  input  d5,
  input  d6,
  input  z,
  output DR_LD1
);

  wire and_1_out, not_1_out, or_1_out;

  and and_1 (and_1_out, d6, z);
  not not_1 (not_1_out, clock);
  or or_1 (or_1_out, d5, and_1_out);
  and and_2 (DR_LD1, t3, not_1_out, or_1_out);
endmodule

module DRBUS0 (
  input  t4,
  input  t6,
  input  d1,
  input  d2,
  output DR_BUs0
);

  wire or_1_out, or_2_out;

  or or_1 (or_1_out, t4, t6);
  or or_2 (or_2_out, d1, d2);
  and and_1 (DR_BUs0, or_1_out, or_2_out);
endmodule

module DRBUS1 (
  input  t4,
  input  d5,
  input  d6,
  input  z,
  output DR_BUS1
);

  wire and_1_out, or_1_out;

  and and_1 (and_1_out, d6, z);
  or or_1 (or_1_out, d5, and_1_out);
  and and_2 (DR_BUS1, t4, or_1_out);
endmodule

module ACC_LD0 (
  input  t3,
  input  clock,
  input  d4,
  input  d8,
  input  d9,
  input  d10,
  output ACCLD0
);

  wire not_1_out, or_1_out;

  not not_1 (not_1_out, clock);
  or or_1 (or_1_out, d4, d8, d9, d10);
  and and_1 (ACCLD0, not_1_out, t3, or_1_out);
endmodule

module ACC_LD1 (
  input  t3,
  input  clock,
  input  d12,
  input  d13,
  input  d14,
  input  d15,
  output ACCLD1
);

  wire not_1_out, or_1_out;

  not not_1 (not_1_out, clock);
  or or_1 (or_1_out, d12, d13, d14, d15);
  and and_1 (ACCLD1, not_1_out, t3, or_1_out);
endmodule

module ACC_LD2 (
  input  t6,
  input  clock,
  input  d1,
  output ACCLD2
);

  wire not_1_out;

  not not_1 (not_1_out, clock);
  and and_1 (ACCLD2, not_1_out, t6, d1);
endmodule

module PC_INC0 (
  input  t1,
  input  t3,
  input  clock,
  input  d1,
  input  d2,
  output PCINC0
);

  wire and_1_out, not_1_out, or_1_out, or_2_out;

  not not_1 (not_1_out, clock);
  and and_1 (and_1_out, t3, or_1_out);
  or or_1 (or_1_out, d1, d2);
  or or_2 (or_2_out, t1, and_1_out);
  and and_2 (PCINC0, not_1_out, or_2_out);
endmodule

module PC_INC1 (
  input  t3,
  input  clock,
  input  d6,
  input  z,
  output PCINC1
);

  wire not_1_out, not_2_out;

  not not_1 (not_1_out, clock);
  not not_2 (not_2_out, z);
  and and_1 (PCINC1, not_1_out, t3, d6, not_2_out);
endmodule
