// Logisim project RSC (5).circ as structural Verilog: 11 circuits, main circuit SC
module SC (
  input  Clock,
  input  Clear,
  output [2:0] SEQ_OUT
);

  wire [2:0] adder_1_out;

  Adder #(.width(3)) adder_1 (.a(SEQ_OUT), .b(3'b001), .out(adder_1_out));  // open: cin, cout
  Register #(.width(3)) register_1 (.D(adder_1_out), .clk(Clock), .Q(SEQ_OUT), .clr(Clear));  // open: en

  // Notes on the sheet:
  //   Counter
  //   Bijay and Kyrillos
  //   Group 6
endmodule

module DecoderCircuit (
  input  [31:0] IR_In,
  output [15:0] D_Out,
  output [3:0] Debug_Instruction
);

  wire or_2_out;
  wire [3:0] or_1_out;
  wire [15:0] decoder_1_out0;

  Decoder #(.select(4)) decoder_1 (
    .out0(decoder_1_out0[0]), .out1(decoder_1_out0[1]), .out2(decoder_1_out0[2]), .out3(decoder_1_out0[3]),
    .out4(decoder_1_out0[4]), .out5(decoder_1_out0[5]), .out6(decoder_1_out0[6]), .out7(decoder_1_out0[7]),
    .out8(decoder_1_out0[8]), .out9(decoder_1_out0[9]), .out10(decoder_1_out0[10]),
    .out11(decoder_1_out0[11]), .out12(decoder_1_out0[12]), .out13(decoder_1_out0[13]),
    .out14(decoder_1_out0[14]), .out15(decoder_1_out0[15]), .sel(IR_In[3:0]));  // open: en
  assign or_1_out = IR_In[7:4] | IR_In[11:8] | IR_In[15:12] | IR_In[19:16] | IR_In[23:20] | IR_In[27:24] | IR_In[31:28];  // OR_Gate or_1, 4 bits wide
  or or_2 (or_2_out, or_1_out[0], or_1_out[1], or_1_out[2], or_1_out[3]);
  Multiplexer #(.width(16)) multiplexer_1 (.in0(decoder_1_out0), .in1({16{1'b0}}), .out(D_Out), .sel(or_2_out));

  assign Debug_Instruction = IR_In[3:0];

  // Notes on the sheet:
  //   Kyrillos Sharkawy Bijay Khanal
  //   Group 6
  //   Decode last 4 bits
endmodule

module TimerCircuit (
  input  Clock,
  input  Clear,
  input  Stop,
  output [7:0] T_Out
);

  wire [2:0] sc_1_seq_out;
  wire [7:0] decoder_1_out0;

  SC sc_1 (.Clock(Clock), .Clear(Clear), .SEQ_OUT(sc_1_seq_out));
  Decoder #(.select(3)) decoder_1 (
    .out0(decoder_1_out0[0]), .out1(decoder_1_out0[1]), .out2(decoder_1_out0[2]), .out3(decoder_1_out0[3]),
    .out4(decoder_1_out0[4]), .out5(decoder_1_out0[5]), .out6(decoder_1_out0[6]), .out7(decoder_1_out0[7]),
    .sel(sc_1_seq_out));  // open: en
  Multiplexer #(.width(8)) multiplexer_1 (.in0(decoder_1_out0), .in1({8{1'b0}}), .out(T_Out), .sel(Stop));
endmodule

module RSC (
  output [7:0] out_1,
  output [3:0] out_2
);

  wire control_1_acc_bus, control_1_acc_clr, control_1_acc_ld, control_1_ar_ld, control_1_dr_bus,
       control_1_dr_ld, control_1_ir_ld, control_1_outr_ld, control_1_pc_bus, control_1_pc_inc,
       control_1_pc_ld, control_1_r_bus, control_1_r_ld, control_1_ram_oe, control_1_ram_we, control_1_z_ld,
       Primary_Clock_out, z_reg_1_z_out;
  wire [2:0] control_1_alu_s;
  wire [31:0] acc_1_data_out, al_u_1_alu_out, ar_1_data_out, dr_1_data_out, ir_1_data_out, outr_1_data_out,
       r_1_bus_out;

  // Probe on ir_1_data_out
  Control control_1 (
    .Clock(Primary_Clock_out), .Z_IN(z_reg_1_z_out), .IR_In(ir_1_data_out), .IR_LD(control_1_ir_ld),
    .R_LD(control_1_r_ld), .T(out_1), .AR_LD(control_1_ar_ld), .D(out_2), .PC_LD(control_1_pc_ld),
    .PC_INC(control_1_pc_inc), .R_BUS(control_1_r_bus), .ACC_CLR(control_1_acc_clr),
    .ACC_BUS(control_1_acc_bus), .Z_LD(control_1_z_ld), .OUTR_LD(control_1_outr_ld),
    .RAM_WE(control_1_ram_we), .DR_LD(control_1_dr_ld), .DR_BUS(control_1_dr_bus), .ACC_LD(control_1_acc_ld),
    .ALU_S(control_1_alu_s), .PC_BUS(control_1_pc_bus), .RAM_OE(control_1_ram_oe));
  Clock Primary_Clock (.out(Primary_Clock_out));
  Z_Reg z_reg_1 (.ACC_IN(acc_1_data_out), .Clock(Primary_Clock_out), .Load(control_1_z_ld), .Z_out(z_reg_1_z_out));
  AR ar_1 (.Data_In(r_1_bus_out), .clock(Primary_Clock_out), .load(control_1_ar_ld), .Data_Out(ar_1_data_out));
  AL_U al_u_1 (
    .A(acc_1_data_out), .B(r_1_bus_out), .S2(control_1_alu_s[2]), .S1(control_1_alu_s[1]),
    .S0(control_1_alu_s[0]), .ALU_Out(al_u_1_alu_out));
  // Probe on ar_1_data_out
  R r_1 (
    .Data_In(r_1_bus_out), .Load(control_1_r_ld), .Clock(Primary_Clock_out), .Bus_Enable(control_1_r_bus),
    .Bus_out(r_1_bus_out));  // open: Data_Out
  // Probe on ar_1_data_out[15:0]
  RAM #(.addrWidth(16), .dataWidth(32), .databus("bidir"), .trigger("high")) ram_1 (
    .addr(ar_1_data_out[15:0]), .we(control_1_ram_we), .oe(control_1_ram_oe), .clk(Primary_Clock_out),
    .data(r_1_bus_out));
  DR dr_1 (
    .Data_In(r_1_bus_out), .Load(control_1_dr_ld), .Clock(Primary_Clock_out), .Bus_Enable(control_1_dr_bus),
    .Data_Out(dr_1_data_out), .Bus_out(r_1_bus_out));
  ACC acc_1 (
    .Data_In(al_u_1_alu_out), .Load(control_1_acc_ld), .Clock(Primary_Clock_out),
    .Bus_Enable(control_1_acc_bus), .Clear(control_1_acc_clr), .Data_Out(acc_1_data_out),
    .Bus_Out(r_1_bus_out));
  PC pc_1 (
    .Data_In(r_1_bus_out), .Count(control_1_pc_inc), .Load(control_1_pc_ld), .Clock(Primary_Clock_out),
    .Bus_Enable(control_1_pc_bus), .Bus_Out(r_1_bus_out));  // open: Data_Out
  OUTR outr_1 (.Data_In(r_1_bus_out), .clock(Primary_Clock_out), .load(control_1_outr_ld), .Data_Out(outr_1_data_out));
  // Probe on dr_1_data_out
  IR ir_1 (.Data_In(dr_1_data_out), .clock(Primary_Clock_out), .load(control_1_ir_ld), .Data_Out(ir_1_data_out));
  Hex_Digit_Display hex_digit_display_1 (.value(outr_1_data_out[31:28]));  // open: dp
  Hex_Digit_Display hex_digit_display_2 (.value(outr_1_data_out[27:24]));  // open: dp
  // Probe on ir_1_data_out
  Hex_Digit_Display hex_digit_display_3 (.value(outr_1_data_out[23:20]));  // open: dp
  Hex_Digit_Display hex_digit_display_4 (.value(outr_1_data_out[19:16]));  // open: dp
  Hex_Digit_Display hex_digit_display_5 (.value(outr_1_data_out[15:12]));  // open: dp
  Hex_Digit_Display hex_digit_display_6 (.value(outr_1_data_out[11:8]));  // open: dp
  Hex_Digit_Display hex_digit_display_7 (.value(outr_1_data_out[7:4]));  // open: dp
  Hex_Digit_Display hex_digit_display_8 (.value(outr_1_data_out[3:0]));  // open: dp

  // Notes on the sheet:
  //        OLA 5
  //   Bijay Khanal and Kyrillos Sharkawy
  //   RSC
endmodule

module Arith_U (
  input  [31:0] A,
  input  [31:0] B,
  input  S1,
  input  S0,
  output [31:0] AU_out
);

  wire and_1_out, nor_1_out;
  wire [31:0] adder_1_out, multiplexer_1_out, not_1_out;

  assign not_1_out = ~B;  // NOT_Gate not_1, 32 bits wide
  Multiplexer #(.select(2), .width(32)) multiplexer_1 (
    .in0(not_1_out), .in1(B), .in2(32'h1), .in3(B), .out(multiplexer_1_out), .sel({S1, S0}));
  nor nor_1 (nor_1_out, S1, S0);
  and and_1 (and_1_out, S1, S0);
  Adder #(.width(32)) adder_1 (.a(A), .b(multiplexer_1_out), .out(adder_1_out), .cin(nor_1_out));  // open: cout
  Multiplexer #(.width(32)) multiplexer_2 (.in0(adder_1_out), .in1(multiplexer_1_out), .out(AU_out), .sel(and_1_out));
endmodule

module Logic_U (
  input  [31:0] B,
  input  [31:0] A,
  input  S0,
  input  S1,
  output [31:0] Logic_Out
);

  wire [31:0] and_1_out, not_1_out, or_1_out, shifter_1_out;

  Shifter #(.shift("ar"), .width(32)) shifter_1 (.in(A), .\dist (5'b00001), .out(shifter_1_out));
  assign not_1_out = ~A;  // NOT_Gate not_1, 32 bits wide
  assign and_1_out = B & A;  // AND_Gate and_1, 32 bits wide
  assign or_1_out = B | A;  // OR_Gate or_1, 32 bits wide
  Multiplexer #(.select(2), .width(32)) multiplexer_1 (
    .in0(and_1_out), .in1(or_1_out), .in2(shifter_1_out), .in3(not_1_out), .out(Logic_Out), .sel({S1, S0}));
endmodule

module AL_U (
  input  [31:0] A,
  input  [31:0] B,
  input  S2,
  input  S1,
  input  S0,
  output [31:0] ALU_Out
);

  wire [31:0] arith_u_1_au_out, logic_u_1_logic_out;

  Arith_U arith_u_1 (.A(A), .B(B), .S1(S1), .S0(S0), .AU_out(arith_u_1_au_out));
  Logic_U logic_u_1 (.B(B), .A(A), .S0(S0), .S1(S1), .Logic_Out(logic_u_1_logic_out));
  Multiplexer #(.width(32)) multiplexer_1 (.in0(arith_u_1_au_out), .in1(logic_u_1_logic_out), .out(ALU_Out), .sel(S2));
endmodule

module Z (
  input  Clock,
  input  Data,
  input  Load,
  output Z_Flag
);

  wire and_1_out, and_2_out, not_1_out;

  not not_1 (not_1_out, Data);
  and and_1 (and_1_out, Data, Load);
  and and_2 (and_2_out, not_1_out, Load);
  J_K_Flip_Flop j_k_ff_1 (
    .J(and_1_out), .clk(Clock), .K(and_2_out), .Q(Z_Flag), .preset(1'b0), .reset(1'b0));  // open: Qn
endmodule

module Control (
  input  Clock,
  input  Z_IN,
  input  [31:0] IR_In,
  output IR_LD,
  output R_LD,
  output [7:0] T,
  output AR_LD,
  output [3:0] D,
  output PC_LD,
  output PC_INC,
  output R_BUS,
  output ACC_CLR,
  output ACC_BUS,
  output Z_LD,
  output OUTR_LD,
  output RAM_WE,
  output DR_LD,
  output DR_BUS,
  output ACC_LD,
  output [2:0] ALU_S,
  output PC_BUS,
  output RAM_OE
);

  wire s_reg_1_data_out, scclr_1_sc_clr, sld_1_s_ld;
  wire [15:0] decodercircuit_1_d_out;

  S_Reg s_reg_1 (.Clock(Clock), .Data(1'b1), .Load(sld_1_s_ld), .Data_Out(s_reg_1_data_out));
  TimerCircuit timercircuit_1 (.Clock(Clock), .Clear(scclr_1_sc_clr), .Stop(s_reg_1_data_out), .T_Out(T));
  SCCLR scclr_1 (
    .t4(T[4]), .t5(T[5]), .t7(T[7]), .d1(decodercircuit_1_d_out[1]), .d2(decodercircuit_1_d_out[2]),
    .d5(decodercircuit_1_d_out[5]), .d6(decodercircuit_1_d_out[6]), .z(Z_IN), .SC_CLR(scclr_1_sc_clr));
  DecoderCircuit decodercircuit_1 (.IR_In(IR_In), .D_Out(decodercircuit_1_d_out), .Debug_Instruction(D));
  SLD sld_1 (.t3(T[3]), .clock(Clock), .d0(decodercircuit_1_d_out[0]), .S_LD(sld_1_s_ld));
  IRLD irld_1 (.t2(T[2]), .clock(Clock), .IR_LD(IR_LD));
  RLD rld_1 (.t3(T[3]), .clock(Clock), .d3(decodercircuit_1_d_out[3]), .R_LD(R_LD));
  ARLD arld_1 (
    .t0(T[0]), .t2(T[2]), .t4(T[4]), .clock(Clock), .d1(decodercircuit_1_d_out[1]),
    .d2(decodercircuit_1_d_out[2]), .AR_LD(AR_LD));
  PCLD pcld_1 (
    .t4(T[4]), .clock(Clock), .d5(decodercircuit_1_d_out[5]), .d6(decodercircuit_1_d_out[6]), .z(Z_IN),
    .PC_LD(PC_LD));
  PCINC pcinc_1 (
    .t1(T[1]), .t3(T[3]), .clock(Clock), .d1(decodercircuit_1_d_out[1]), .d2(decodercircuit_1_d_out[2]),
    .d6(decodercircuit_1_d_out[6]), .z(Z_IN), .PC_INC(PC_INC));
  RBUS rbus_1 (
    .t3(T[3]), .d4(decodercircuit_1_d_out[4]), .d8(decodercircuit_1_d_out[8]),
    .d9(decodercircuit_1_d_out[9]), .d12(decodercircuit_1_d_out[12]), .d13(decodercircuit_1_d_out[13]),
    .R_BUS(R_BUS));
  ACCCLR accclr_1 (.t3(T[3]), .d11(decodercircuit_1_d_out[11]), .ACC_CLR(ACC_CLR));
  ACCBUS accbus_1 (
    .t3(T[3]), .t5(T[5]), .d2(decodercircuit_1_d_out[2]), .d3(decodercircuit_1_d_out[3]),
    .d7(decodercircuit_1_d_out[7]), .ACC_BUS(ACC_BUS));
  ZLD zld_1 (.Z_LD(Z_LD));
  OUTRLD outrld_1 (.t3(T[3]), .clock(Clock), .d7(decodercircuit_1_d_out[7]), .OUTR_LD(OUTR_LD));
  RAMRW ramrw_1 (.t2(T[2]), .clock(Clock), .d6(decodercircuit_1_d_out[6]), .RAM_WE(RAM_WE));
  DRLD drld_1 (
    .t1(T[1]), .t3(T[3]), .t5(T[5]), .clock(Clock), .d1(decodercircuit_1_d_out[1]),
    .d2(decodercircuit_1_d_out[2]), .d5(decodercircuit_1_d_out[5]), .d6(decodercircuit_1_d_out[6]), .z(Z_IN),
    .DR_LD(DR_LD));
  DRBUS drbus_1 (
    .t4(T[4]), .t6(T[6]), .d1(decodercircuit_1_d_out[1]), .d2(decodercircuit_1_d_out[2]),
    .d5(decodercircuit_1_d_out[5]), .d6(decodercircuit_1_d_out[6]), .z(Z_IN), .DR_BUS(DR_BUS));
  ACCLD accld_1 (
    .t3(T[3]), .t6(T[6]), .clock(Clock), .d1(decodercircuit_1_d_out[1]), .d4(decodercircuit_1_d_out[4]),
    .d8(decodercircuit_1_d_out[8]), .d9(decodercircuit_1_d_out[9]), .d10(decodercircuit_1_d_out[10]),
    .d12(decodercircuit_1_d_out[12]), .d13(decodercircuit_1_d_out[13]), .d14(decodercircuit_1_d_out[14]),
    .d15(decodercircuit_1_d_out[15]), .ACC_LD(ACC_LD));
  ALU_SEL alu_sel_1 (
    .d1(decodercircuit_1_d_out[1]), .d4(decodercircuit_1_d_out[4]), .d9(decodercircuit_1_d_out[9]),
    .d10(decodercircuit_1_d_out[10]), .d12(decodercircuit_1_d_out[12]), .d13(decodercircuit_1_d_out[13]),
    .d14(decodercircuit_1_d_out[14]), .d15(decodercircuit_1_d_out[15]), .s0(ALU_S[0]), .s1(ALU_S[1]),
    .s2(ALU_S[2]));
  PCBUS pcbus_1 (.t0(T[0]), .t2(T[2]), .PC_BUS(PC_BUS));
  RAMEN ramen_1 (
    .t1(T[1]), .t3(T[3]), .t5(T[5]), .clock(Clock), .d1(decodercircuit_1_d_out[1]),
    .d2(decodercircuit_1_d_out[2]), .d5(decodercircuit_1_d_out[5]), .d6(decodercircuit_1_d_out[6]), .z(Z_IN),
    .RAM_OE(RAM_OE));

  // Notes on the sheet:
  //   T-sig
  //   D-Sig
  //   Z
endmodule

module S_Reg (
  input  Clock,
  input  Data,
  input  Load,
  output Data_Out
);

  wire and_1_out, and_2_out, not_1_out;

  and and_1 (and_1_out, Data, Load);
  not not_1 (not_1_out, Data);
  and and_2 (and_2_out, not_1_out, Load);
  J_K_Flip_Flop j_k_ff_1 (.J(and_1_out), .K(and_2_out), .clk(Clock), .Q(Data_Out), .preset(1'b0));  // open: Qn, reset
endmodule

module Z_Reg (
  input  [31:0] ACC_IN,
  input  Clock,
  input  Load,
  output Z_out
);

  wire not_1_out, or_1_out;

  or or_1 (or_1_out, ACC_IN[0], ACC_IN[1], ACC_IN[2], ACC_IN[3], ACC_IN[4], ACC_IN[5], ACC_IN[6], ACC_IN[7], ACC_IN[8], ACC_IN[9], ACC_IN[10], ACC_IN[11], ACC_IN[12], ACC_IN[13], ACC_IN[14], ACC_IN[15], ACC_IN[16], ACC_IN[17], ACC_IN[18], ACC_IN[19], ACC_IN[20], ACC_IN[21], ACC_IN[22], ACC_IN[23], ACC_IN[24], ACC_IN[25], ACC_IN[26], ACC_IN[27], ACC_IN[28], ACC_IN[29], ACC_IN[30], ACC_IN[31]);
  not not_1 (not_1_out, or_1_out);
  Onebit_reg onebit_reg_1 (.Clock(Clock), .Data(not_1_out), .Clear(1'b0), .Load(Load), .Data_Out(Z_out));
endmodule
