// Logisim project custom_reg.circ as structural Verilog: 2 circuits, main circuit Onebit_reg
module Onebit_reg (
  input  Clock,
  input  Data,
  input  Clear,
  input  Load,
  output Data_Out
);

  wire and_1_out, and_2_out, not_1_out;

  and and_1 (and_1_out, Data, Load);
  not not_1 (not_1_out, Data);
  and and_2 (and_2_out, not_1_out, Load);
  J_K_Flip_Flop j_k_ff_1 (
    .J(and_1_out), .K(and_2_out), .clk(Clock), .Q(Data_Out), .preset(1'b0), .reset(Clear));  // open: Qn

  // Notes on the sheet:
  //   One bit Register
endmodule

module BasicRegister (
  input  [7:0] in_1,
  input  in_2,
  input  in_3,
  input  in_4,
  output [7:0] out_5
);

  wire [7:0] register_1_q;

  Register register_1 (.D(in_1), .en(in_2), .clk(in_4), .Q(register_1_q));  // open: clr
  assign out_5 = in_3 ? register_1_q : 8'bz;  // Controlled_Buffer controlled_buffer_1
endmodule
